# Fritzing sketch laserspike (saved by Fritzing 0.9.3b)

parts:
  Part1 = Adafruit MAX4466 Electret Microphone Amplifier [part_number="Adafruit #1063"]
  Part2 = 16-Channel 12-bit PWM Servo Driver - I2C [part_number=815]
  Part5 = Arduino Nano (Rev3.0)
  Q24 = NPN-Transistor [package="TO92 [THT]"]
  Q25 = NPN-Transistor [package="TO92 [THT]"]
  Q26 = NPN-Transistor [package="TO92 [THT]"]
  Q27 = NPN-Transistor [package="TO92 [THT]"]
  Q28 = NPN-Transistor [package="TO92 [THT]"]
  Q29 = NPN-Transistor [package="TO92 [THT]"]
  Q30 = NPN-Transistor [package="TO92 [THT]"]
  Q31 = NPN-Transistor [package="TO92 [THT]"]
  LED1 = LED - 5mm [color="Red (633nm)" package="5 mm [THT]"]
  LED2 = LED - 5mm [color="Red (633nm)" package="5 mm [THT]"]
  LED3 = LED - 5mm [color="Red (633nm)" package="5 mm [THT]"]
  LED4 = LED - 5mm [color="Red (633nm)" package="5 mm [THT]"]
  LED5 = LED - 5mm [color="Red (633nm)" package="5 mm [THT]"]
  LED6 = LED - 5mm [color="Red (633nm)" package="5 mm [THT]"]
  LED7 = LED - 5mm [color="Red (633nm)" package="5 mm [THT]"]
  LED8 = LED - 5mm [color="Red (633nm)" package="5 mm [THT]"]
  LED9 = LED - 5mm [color="Red (633nm)" package="5 mm [THT]"]
  LED10 = LED - 5mm [color="Red (633nm)" package="5 mm [THT]"]
  LED11 = LED - 5mm [color="Red (633nm)" package="5 mm [THT]"]
  LED12 = LED - 5mm [color="Red (633nm)" package="5 mm [THT]"]
  LED13 = LED - 5mm [color="Red (633nm)" package="5 mm [THT]"]
  LED14 = LED - 5mm [color="Red (633nm)" package="5 mm [THT]"]
  LED15 = LED - 5mm [color="Red (633nm)" package="5 mm [THT]"]
  LED16 = LED - 5mm [color="Red (633nm)" package="5 mm [THT]"]
  LED17 = LED - 5mm [color="Red (633nm)" package="5 mm [THT]"]
  LED18 = LED - 5mm [color="Red (633nm)" package="5 mm [THT]"]
  LED19 = LED - 5mm [color="Red (633nm)" package="5 mm [THT]"]
  LED20 = LED - 5mm [color="Red (633nm)" package="5 mm [THT]"]
  LED21 = LED - 5mm [color="Red (633nm)" package="5 mm [THT]"]
  LED22 = LED - 5mm [color="Red (633nm)" package="5 mm [THT]"]
  LED23 = LED - 5mm [color="Red (633nm)" package="5 mm [THT]"]
  LED24 = LED - 5mm [color="Red (633nm)" package="5 mm [THT]"]
  LED25 = LED - 5mm [color="Red (633nm)" package="5 mm [THT]"]
  LED26 = LED - 5mm [color="Red (633nm)" package="5 mm [THT]"]
  LED27 = LED - 5mm [color="Red (633nm)" package="5 mm [THT]"]
  LED28 = LED - 5mm [color="Red (633nm)" package="5 mm [THT]"]
  LED29 = LED - 5mm [color="Red (633nm)" package="5 mm [THT]"]
  LED30 = LED - 5mm [color="Red (633nm)" package="5 mm [THT]"]
  LED31 = LED - 5mm [color="Red (633nm)" package="5 mm [THT]"]
  LED32 = LED - 5mm [color="Red (633nm)" package="5 mm [THT]"]
  LED33 = LED - 5mm [color="Red (633nm)" package="5 mm [THT]"]
  LED35 = LED - 5mm [color="Red (633nm)" package="5 mm [THT]"]
  LED36 = LED - 5mm [color="Red (633nm)" package="5 mm [THT]"]
  LED37 = LED - 5mm [color="Red (633nm)" package="5 mm [THT]"]
  LED38 = LED - 5mm [color="Red (633nm)" package="5 mm [THT]"]
  LED40 = LED - 5mm [color="Red (633nm)" package="5 mm [THT]"]
  LED43 = LED - 5mm [color="Red (633nm)" package="5 mm [THT]"]
  LED44 = LED - 5mm [color="Red (633nm)" package="5 mm [THT]"]
  LED45 = LED - 5mm [color="Red (633nm)" package="5 mm [THT]"]
  LED46 = LED - 5mm [color="Red (633nm)" package="5 mm [THT]"]
  LED48 = LED - 5mm [color="Red (633nm)" package="5 mm [THT]"]
  LED50 = LED - 5mm [color="Red (633nm)" package="5 mm [THT]"]
  LED52 = LED - 5mm [color="Red (633nm)" package="5 mm [THT]"]
  LED53 = LED - 5mm [color="Red (633nm)" package="5 mm [THT]"]
  LED54 = LED - 5mm [color="Red (633nm)" package="5 mm [THT]"]
  LED55 = LED - 5mm [color="Red (633nm)" package="5 mm [THT]"]
  LED56 = LED - 5mm [color="Red (633nm)" package="5 mm [THT]"]
  LED57 = LED - 5mm [color="Red (633nm)" package="5 mm [THT]"]
  LED58 = LED - 5mm [color="Red (633nm)" package="5 mm [THT]"]
  LED59 = LED - 5mm [color="Red (633nm)" package="5 mm [THT]"]
  LED60 = LED - 5mm [color="Red (633nm)" package="5 mm [THT]"]
  LED62 = LED - 5mm [color="Red (633nm)" package="5 mm [THT]"]
  LED63 = LED - 5mm [color="Red (633nm)" package="5 mm [THT]"]
  LED64 = LED - 5mm [color="Red (633nm)" package="5 mm [THT]"]
  Q19 = NPN-Transistor [package="TO92 [THT]"]
  Q9 = NPN-Transistor [package="TO92 [THT]"]
  Q18 = NPN-Transistor [package="TO92 [THT]"]
  Q23 = NPN-Transistor [package="TO92 [THT]"]
  Q17 = NPN-Transistor [package="TO92 [THT]"]
  Q20 = NPN-Transistor [package="TO92 [THT]"]
  Q22 = NPN-Transistor [package="TO92 [THT]"]
  Q21 = NPN-Transistor [package="TO92 [THT]"]
  BATT1 = LiPoly Battery (1300mAh)
  M1 = RioRand LM2596
  M2 = RioRand LM2596
  LED65 = LED - 5mm [color="Red (633nm)" package="5 mm [THT]"]
  LED66 = LED - 5mm [color="Red (633nm)" package="5 mm [THT]"]
  LED67 = LED - 5mm [color="Red (633nm)" package="5 mm [THT]"]
  LED68 = LED - 5mm [color="Red (633nm)" package="5 mm [THT]"]
  LED69 = LED - 5mm [color="Red (633nm)" package="5 mm [THT]"]
  LED70 = LED - 5mm [color="Red (633nm)" package="5 mm [THT]"]
  LED71 = LED - 5mm [color="Red (633nm)" package="5 mm [THT]"]
  LED72 = LED - 5mm [color="Red (633nm)" package="5 mm [THT]"]
  Part6 = 16-Channel 12-bit PWM Servo Driver - I2C [part_number=815]
  Q32 = NPN-Transistor [package="TO92 [THT]"]
  Q33 = NPN-Transistor [package="TO92 [THT]"]
  Q34 = NPN-Transistor [package="TO92 [THT]"]
  Q35 = NPN-Transistor [package="TO92 [THT]"]
  Q36 = NPN-Transistor [package="TO92 [THT]"]
  Q37 = NPN-Transistor [package="TO92 [THT]"]
  Q38 = NPN-Transistor [package="TO92 [THT]"]
  Q39 = NPN-Transistor [package="TO92 [THT]"]
  Q40 = NPN-Transistor [package="TO92 [THT]"]
  Q41 = NPN-Transistor [package="TO92 [THT]"]
  Q42 = NPN-Transistor [package="TO92 [THT]"]
  Q43 = NPN-Transistor [package="TO92 [THT]"]
  Q44 = NPN-Transistor [package="TO92 [THT]"]
  Q45 = NPN-Transistor [package="TO92 [THT]"]
  Q46 = NPN-Transistor [package="TO92 [THT]"]
  LED73 = LED - 5mm [color="Red (633nm)" package="5 mm [THT]"]
  LED74 = LED - 5mm [color="Red (633nm)" package="5 mm [THT]"]
  LED75 = LED - 5mm [color="Red (633nm)" package="5 mm [THT]"]
  LED76 = LED - 5mm [color="Red (633nm)" package="5 mm [THT]"]
  LED77 = LED - 5mm [color="Red (633nm)" package="5 mm [THT]"]
  LED78 = LED - 5mm [color="Red (633nm)" package="5 mm [THT]"]
  LED79 = LED - 5mm [color="Red (633nm)" package="5 mm [THT]"]
  LED80 = LED - 5mm [color="Red (633nm)" package="5 mm [THT]"]
  LED81 = LED - 5mm [color="Red (633nm)" package="5 mm [THT]"]
  LED82 = LED - 5mm [color="Red (633nm)" package="5 mm [THT]"]
  LED83 = LED - 5mm [color="Red (633nm)" package="5 mm [THT]"]
  LED84 = LED - 5mm [color="Red (633nm)" package="5 mm [THT]"]
  LED85 = LED - 5mm [color="Red (633nm)" package="5 mm [THT]"]
  LED86 = LED - 5mm [color="Red (633nm)" package="5 mm [THT]"]
  LED87 = LED - 5mm [color="Red (633nm)" package="5 mm [THT]"]
  LED88 = LED - 5mm [color="Red (633nm)" package="5 mm [THT]"]
  LED89 = LED - 5mm [color="Red (633nm)" package="5 mm [THT]"]
  LED90 = LED - 5mm [color="Red (633nm)" package="5 mm [THT]"]
  LED91 = LED - 5mm [color="Red (633nm)" package="5 mm [THT]"]
  LED92 = LED - 5mm [color="Red (633nm)" package="5 mm [THT]"]
  LED93 = LED - 5mm [color="Red (633nm)" package="5 mm [THT]"]
  LED94 = LED - 5mm [color="Red (633nm)" package="5 mm [THT]"]
  LED95 = LED - 5mm [color="Red (633nm)" package="5 mm [THT]"]
  LED96 = LED - 5mm [color="Red (633nm)" package="5 mm [THT]"]
  LED97 = LED - 5mm [color="Red (633nm)" package="5 mm [THT]"]
  LED98 = LED - 5mm [color="Red (633nm)" package="5 mm [THT]"]
  LED99 = LED - 5mm [color="Red (633nm)" package="5 mm [THT]"]
  LED100 = LED - 5mm [color="Red (633nm)" package="5 mm [THT]"]
  LED101 = LED - 5mm [color="Red (633nm)" package="5 mm [THT]"]
  LED102 = LED - 5mm [color="Red (633nm)" package="5 mm [THT]"]
  LED103 = LED - 5mm [color="Red (633nm)" package="5 mm [THT]"]
  LED104 = LED - 5mm [color="Red (633nm)" package="5 mm [THT]"]
  LED105 = LED - 5mm [color="Red (633nm)" package="5 mm [THT]"]
  LED106 = LED - 5mm [color="Red (633nm)" package="5 mm [THT]"]
  LED107 = LED - 5mm [color="Red (633nm)" package="5 mm [THT]"]
  LED108 = LED - 5mm [color="Red (633nm)" package="5 mm [THT]"]
  LED109 = LED - 5mm [color="Red (633nm)" package="5 mm [THT]"]
  LED110 = LED - 5mm [color="Red (633nm)" package="5 mm [THT]"]
  LED111 = LED - 5mm [color="Red (633nm)" package="5 mm [THT]"]
  LED112 = LED - 5mm [color="Red (633nm)" package="5 mm [THT]"]
  LED113 = LED - 5mm [color="Red (633nm)" package="5 mm [THT]"]
  LED114 = LED - 5mm [color="Red (633nm)" package="5 mm [THT]"]
  LED115 = LED - 5mm [color="Red (633nm)" package="5 mm [THT]"]
  LED116 = LED - 5mm [color="Red (633nm)" package="5 mm [THT]"]
  LED117 = LED - 5mm [color="Red (633nm)" package="5 mm [THT]"]
  LED118 = LED - 5mm [color="Red (633nm)" package="5 mm [THT]"]
  LED119 = LED - 5mm [color="Red (633nm)" package="5 mm [THT]"]
  LED120 = LED - 5mm [color="Red (633nm)" package="5 mm [THT]"]
  LED121 = LED - 5mm [color="Red (633nm)" package="5 mm [THT]"]
  LED122 = LED - 5mm [color="Red (633nm)" package="5 mm [THT]"]
  LED123 = LED - 5mm [color="Red (633nm)" package="5 mm [THT]"]
  LED124 = LED - 5mm [color="Red (633nm)" package="5 mm [THT]"]
  LED125 = LED - 5mm [color="Red (633nm)" package="5 mm [THT]"]
  LED126 = LED - 5mm [color="Red (633nm)" package="5 mm [THT]"]
  LED127 = LED - 5mm [color="Red (633nm)" package="5 mm [THT]"]
  LED128 = LED - 5mm [color="Red (633nm)" package="5 mm [THT]"]
  LED129 = LED - 5mm [color="Red (633nm)" package="5 mm [THT]"]
  LED130 = LED - 5mm [color="Red (633nm)" package="5 mm [THT]"]
  LED131 = LED - 5mm [color="Red (633nm)" package="5 mm [THT]"]
  LED132 = LED - 5mm [color="Red (633nm)" package="5 mm [THT]"]
  LED133 = LED - 5mm [color="Red (633nm)" package="5 mm [THT]"]
  LED134 = LED - 5mm [color="Red (633nm)" package="5 mm [THT]"]
  LED135 = LED - 5mm [color="Red (633nm)" package="5 mm [THT]"]
  LED136 = LED - 5mm [color="Red (633nm)" package="5 mm [THT]"]
  Q47 = NPN-Transistor [package="TO92 [THT]"]
  Part7 = Adafruit Analog 2-Axis Joystick [part_number="Adafruit #512"]
  F1 = FUSE [package=fuse_5mm]
  S1 = Taiway 100-SP-X-T1 SPDT Miniature Toggle Switch [part_number=100-SP-X-T1-0-0-B1-M1 package=THT]

nets:
  VCC: Part1.VCC, Part2.VCC, Part5.VIN, M2.Pin_3, Part6.VCC, Part7.VCC
  GND: Part1.GND, Part2.GND, Part5.GND, LED1.cathode, LED3.cathode, LED4.cathode, LED6.cathode, LED7.cathode, LED8.cathode, LED9.cathode, LED10.cathode, LED11.cathode, LED12.cathode, LED13.cathode, LED14.cathode, LED15.cathode, LED16.cathode, LED17.cathode, LED18.cathode, LED19.cathode, LED20.cathode, LED21.cathode, LED22.cathode, LED23.cathode, LED24.cathode, LED25.cathode, LED26.cathode, LED27.cathode, LED28.cathode, LED29.cathode, LED30.cathode, LED31.cathode, LED32.cathode, LED33.cathode, LED35.cathode, LED36.cathode, LED37.cathode, LED38.cathode, LED40.cathode, LED43.cathode, LED44.cathode, LED45.cathode, LED46.cathode, LED48.cathode, LED50.cathode, LED52.cathode, LED53.cathode, LED54.cathode, LED55.cathode, LED56.cathode, LED57.cathode, LED58.cathode, LED59.cathode, LED60.cathode, LED62.cathode, LED63.cathode, LED64.cathode, M1.Pin_4, M2.Pin_4, LED66.cathode, LED67.cathode, LED68.cathode, LED70.cathode, LED71.cathode, LED72.cathode, Part6.GND, LED73.cathode, LED74.cathode, LED75.cathode, LED76.cathode, LED77.cathode, LED78.cathode, LED79.cathode, LED80.cathode, LED81.cathode, LED82.cathode, LED83.cathode, LED85.cathode, LED86.cathode, LED87.cathode, LED88.cathode, LED90.cathode, LED91.cathode, LED92.cathode, LED93.cathode, LED94.cathode, LED95.cathode, LED96.cathode, LED97.cathode, LED98.cathode, LED99.cathode, LED100.cathode, LED101.cathode, LED102.cathode, LED103.cathode, LED104.cathode, LED105.cathode, LED106.cathode, LED107.cathode, LED108.cathode, LED109.cathode, LED110.cathode, LED111.cathode, LED113.cathode, LED114.cathode, LED115.cathode, LED116.cathode, LED118.cathode, LED119.cathode, LED121.cathode, LED122.cathode, LED123.cathode, LED124.cathode, LED125.cathode, LED126.cathode, LED127.cathode, LED128.cathode, LED129.cathode, LED130.cathode, LED131.cathode, LED132.cathode, LED133.cathode, LED134.cathode, LED135.cathode, LED136.cathode, Part7.GND
  N1: Part1.OUT, Part5.A0
  N2: Part2.PWRIN, Q34.B
  N3: Part2.PWM7, Q31.C
  N4: Part2.PWM6, Q28.C
  N5: Part2.PWM5, Q30.C
  N6: Part2.PWM4, Q29.C
  N7: Part2.PWM3, Q27.C
  N8: Part2.PWM2, Q26.C
  N9: Part2.PWM1, Q25.C
  N10: Part2.PWM0, Q24.C
  N11: Part2.5.0V, Part6.5.0V
  N12: Part2.SDA, Part5.A4, Part6.SDA
  N13: Part2.SCL, Part5.A5, Part6.SCL
  N14: Part2.OE, Part6.OE
  N15: Part2.PWM15, Q20.C
  N16: Part2.PWM14, Q22.C
  N17: Part2.PWM13, Q23.C
  N18: Part2.PWM12, Q21.C
  N19: Part2.PWM11, Q9.C
  N20: Part2.PWM10, Q17.C
  N21: Part2.PWM9, Q18.C
  N22: Part2.PWM8, Q19.C
  N23: Part5.D4, Part7.SWITCH
  N24: Part5.A2, Part7.YOUT
  N25: Part5.A1, Part7.XOUT
  N26: Q24.E, LED35.anode, LED36.anode, LED40.anode, LED43.anode
  N27: Q24.B, Q25.B, Q26.B, Q27.B, Q28.B, Q29.B, Q30.B, Q31.B, Q19.B, Q9.B, Q18.B, Q23.B, Q17.B, Q20.B, Q22.B, Q21.B, M1.Pin_3, Part6.PWRIN, Q32.B, Q33.B, Q35.B, Q36.B, Q37.B, Q38.B, Q39.B, Q40.B, Q41.B, Q42.B, Q43.B, Q44.B, Q45.B, Q46.B, Q47.B
  N28: Q25.E, LED33.anode, LED48.anode, LED62.anode, LED64.anode
  N29: Q26.E, LED38.anode, LED52.anode, LED56.anode, LED59.anode
  N30: Q27.E, LED65.anode, LED67.anode, LED69.anode, LED71.anode
  N31: Q28.E, LED37.anode, LED44.anode, LED46.anode, LED57.anode
  N32: Q29.E, LED45.anode, LED54.anode, LED60.anode, LED63.anode
  N33: Q30.E, LED50.anode, LED53.anode, LED55.anode, LED58.anode
  N34: Q31.E, LED66.anode, LED68.anode, LED70.anode, LED72.anode
  N35: LED1.anode, LED6.anode, LED11.anode, LED15.anode, Q22.E
  N36: LED2.cathode, LED5.cathode
  N37: LED2.anode, LED5.anode, LED10.anode, LED14.anode, Q20.E
  N38: LED3.anode, LED8.anode, LED12.anode, LED16.anode, Q23.E
  N39: LED4.anode, LED7.anode, LED9.anode, LED13.anode, Q21.E
  N40: LED17.anode, LED21.anode, LED26.anode, LED32.anode, Q18.E
  N41: LED18.anode, LED20.anode, LED22.anode, LED25.anode, Q9.E
  N42: LED19.anode, LED27.anode, LED28.anode, LED29.anode, Q19.E
  N43: LED23.anode, LED24.anode, LED30.anode, LED31.anode, Q17.E
  N44: BATT1.positive, F1.2
  N45: BATT1.negative, M1.Pin_2, M2.Pin_2
  N46: M1.Pin_1, M2.Pin_1, S1.L2
  N47: LED65.cathode, LED69.cathode
  N48: Part6.PWM7, Q42.C
  N49: Part6.PWM6, Q46.C
  N50: Part6.PWM5, Q43.C
  N51: Part6.PWM4, Q45.C
  N52: Part6.PWM3, Q44.C
  N53: Part6.PWM2, Q41.C
  N54: Part6.PWM1, Q40.C
  N55: Part6.PWM0, Q39.C
  N56: Part6.PWM15, Q47.C
  N57: Part6.PWM14, Q36.C
  N58: Part6.PWM13, Q34.C
  N59: Part6.PWM12, Q38.C
  N60: Part6.PWM11, Q33.C
  N61: Part6.PWM10, Q35.C
  N62: Part6.PWM9, Q32.C
  N63: Part6.PWM8, Q37.C
  N64: Q32.E, LED104.anode, LED125.anode, LED131.anode, LED132.anode
  N65: Q33.E, LED128.anode, LED130.anode, LED133.anode, LED135.anode
  N66: Q34.E, LED105.anode, LED107.anode, LED113.anode, LED114.anode
  N67: Q35.E, LED121.anode, LED124.anode, LED134.anode, LED136.anode
  N68: Q36.E, LED103.anode, LED109.anode, LED111.anode, LED118.anode
  N69: Q37.E, LED120.anode, LED122.anode, LED123.anode, LED129.anode
  N70: Q38.E, LED106.anode, LED110.anode, LED115.anode, LED116.anode
  N71: Q39.E, LED81.anode, LED83.anode, LED119.anode, LED126.anode
  N72: Q40.E, LED73.anode, LED96.anode, LED100.anode, LED127.anode
  N73: Q41.E, LED77.anode, LED79.anode, LED94.anode, LED97.anode
  N74: Q42.E, LED85.anode, LED88.anode, LED90.anode, LED91.anode
  N75: Q43.E, LED74.anode, LED76.anode, LED87.anode, LED95.anode
  N76: Q44.E, LED84.anode, LED86.anode, LED89.anode, LED92.anode
  N77: Q45.E, LED78.anode, LED80.anode, LED98.anode, LED99.anode
  N78: Q46.E, LED75.anode, LED82.anode, LED93.anode, LED101.anode
  N79: LED84.cathode, LED89.cathode
  N80: LED102.anode, LED108.anode, LED112.anode, LED117.anode, Q47.E
  N81: LED112.cathode, LED117.cathode
  N82: F1.1, S1.L1

notes:
  LEDs are used in place of the laser diodes
  I've used a 5V 3A BEC for the laser diode power supply
  I've used a 3A automotive fuse
  A 3s LiPo battery (11.1V, 1.3A) will last a few hours

custom parts:
  Adafruit MAX4466 Electret Microphone Amplifier: Add an ear to your project with this well-designed electret microphone amplifier. This fully assembled and tested board comes with a 20-20KHz electret microphone soldered on. For the amplification, we use the Maxim MAX4466, an op-amp specifically designed for this delicate task! The amplifier has excellent power supply noise rejection, so this amplifier sounds really good and isn't nearly as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
  16-Channel 12-bit PWM Servo Driver - I2C: You want to make a cool robot, maybe a hexapod walker, or maybe just a piece of art with a lot of moving parts. Or maybe you want to drive a lot of LEDs with precise PWM output. Using only two pins, control 16 free-running PWM outputs! You can even chain up 62 breakouts to control up to 992 PWM outputs.
  LiPoly Battery (1300mAh): Lithium Ion Polymer Battery (1300mAh)
  Adafruit Analog 2-Axis Joystick: This mini-kit makes it easy to mount a PSP/Xbox-like thumb joystick to your project. The thumbstick is an analog joystick - more accurate and sensitive than just 'directional' joysticks - with a 'press in to select' button. Since it's analog, you'll need two analog reading pins on your microcontroller to determine X and Y. Having an extra digital input will let you read the switch. The pack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
